// Digital circuit FinalProject.dig as structural Verilog
module FinalProject (
  input  [7:0] M,
  input  [7:0] N,
  input  [12:0] progIN,
  input  reset,
  input  progLoad,
  input  start,
  input  result,
  input  clk,
  output valid,
  output done,
  output [7:0] \output ,
  output [7:0] Operand,
  output [4:0] Opcode,
  output [7:0] Adress,
  output out_15,
  output [7:0] out_16,
  output [7:0] out_17,
  output [7:0] out_18,
  output [7:0] Adress_2,
  output [7:0] Adress_3,
  output [7:0] m_2,
  output [7:0] n_2
);

  wire accA____accA__lt__lt__accB, accA____accA_AND_accB, accA____accA_OR_accB, accA____accA_XOR_accB,
       accA___accA___accB, accA___accA___accB_t, accA___accA___accB_t_t, accA___accA___accB_t_t_t,
       accA___accA___accB_t_t_t_t, accA___accA__plus__accB, accA___accB, accA___NOT_accA, accA___Operand,
       accA___pRAM_adr_Operand, accA___regC, accA___rRAM_adr_Operand, accA_CMP_accB, accB___accA,
       accB___Operand, and_1_out, and_2_out, and_3_out, and_4_out, and_5_out, comparator_4_gt,
       comparator_4_lt, comparator_5_gt, comparator_5_lt, d_ff_10_q, delay_1_out, ef, \end , end_reset,
       equal, finishfuture, FUTURE, gf, greather, isPrime_accA, jump_if, Jump_to_address_Operand,
       Jump_to_address_Operand_if_eq, Jump_to_address_Operand_if_eq_or_gr, Jump_to_address_Operand_if_gr,
       Jump_to_address_Operand_if_le, less, lf, multiplexer_4_out, multiplexer_5_out, multiplexer_6_out,
       multiplexer_7_out, multiplexer_8_out, multiplexer_9_out, multiplexer_10_out, multiplexer_11_out,
       multiplexer_12_out, multiplexer_16_out, multiplexer_20_out, multiplexer_21_out, multiplexer_22_out,
       multiplexer_23_out, multiplexer_24_out, multiplexer_25_out, multiplexer_26_out, multiplexer_27_out,
       multiplexer_29_out, multiplexer_31_out, multiplexer_33_out, multiplexer_35_out, multiplexer_36_out,
       multiplexer_37_out, newA_if, newB_if, newC_if, or_1_out, or_2_out, or_3_out, or_5_out, or_6_out,
       or_7_out, or_8_out, or_9_out, or_10_out, or_15_out, or_16_out, prime, process, process_reset,
       process_rRAM, readyin, regC___accA, regC___M, regC___N, rRAM_adr_Operand____accA, stop, switch_to_2,
       xor_1_out, xor_2_out, xor_3_out, xor_6_out;
  wire [7:0] \and , Futureaddress, Futureinput, multiplexer_1_out, multiplexer_2_out, multiplexer_3_out,
       multiplexer_13_out, multiplexer_14_out, multiplexer_15_out, multiplexer_17_out, multiplexer_19_out,
       multiplexer_28_out, multiplexer_30_out, multiplexer_32_out, newA, \not , \or , Output_t, plus,
       rRAMout, shift_left, tunnel, tunnel_t, tunnel_t_t, tunnel_t_t_t, tunnel_t_t_t_t, \xor ;
  wire [12:0] delay_2_out, pRAM;
  wire [15:0] rom_2_d;

  or or_1 (or_1_out, result, process_rRAM);
  CounterPreset #(.maxValue(15), .Bits(8)) counterpreset_1 (
    .en(or_1_out), .C(clk), .dir(1'b0), .in(8'h1), .ld(1'b0), .clr(result), .out(Adress_2));  // open: ovf
  Comparator #(.Bits(8)) comparator_1 (.a(Adress_2), .b(8'hf), .eq(\end ));  // open: gt, lt
  Multiplexer #(.Bits(8)) multiplexer_1 (
    .sel(rRAM_adr_Operand____accA), .in_0(Adress_2), .in_1(Operand), .out(multiplexer_1_out));
  Multiplexer #(.Bits(8)) multiplexer_2 (
    .sel(or_2_out), .in_0(multiplexer_1_out), .in_1(Adress_3), .out(multiplexer_2_out));
  or or_2 (or_2_out, reset, process_reset);
  Multiplexer #(.Bits(8)) multiplexer_3 (
    .sel(FUTURE), .in_0(multiplexer_2_out), .in_1(Futureaddress), .out(multiplexer_3_out));
  or or_3 (or_3_out, ef, gf);
  Multiplexer multiplexer_4 (.sel(accA_CMP_accB), .in_0(gf), .in_1(greather), .out(multiplexer_4_out));
  Multiplexer multiplexer_5 (.sel(accA_CMP_accB), .in_0(ef), .in_1(equal), .out(multiplexer_5_out));
  Multiplexer multiplexer_6 (.sel(accA_CMP_accB), .in_0(lf), .in_1(less), .out(multiplexer_6_out));
  Multiplexer multiplexer_7 (.sel(isPrime_accA), .in_0(multiplexer_5_out), .in_1(prime), .out(multiplexer_7_out));
  Multiplexer multiplexer_8 (.sel(reset), .in_0(multiplexer_6_out), .in_1(1'b0), .out(multiplexer_8_out));
  and and_1 (and_1_out, Jump_to_address_Operand_if_eq, ef);
  and and_2 (and_2_out, Jump_to_address_Operand_if_gr, gf);
  and and_3 (and_3_out, Jump_to_address_Operand_if_le, lf);
  and and_4 (and_4_out, Jump_to_address_Operand_if_eq_or_gr, or_3_out);
  Multiplexer multiplexer_9 (.sel(reset), .in_0(multiplexer_4_out), .in_1(1'b0), .out(multiplexer_9_out));
  Multiplexer multiplexer_10 (.sel(reset), .in_0(multiplexer_7_out), .in_1(1'b0), .out(multiplexer_10_out));
  Multiplexer multiplexer_11 (.sel(\end ), .in_0(process_rRAM), .in_1(1'b0), .out(multiplexer_11_out));
  Multiplexer multiplexer_12 (.sel(or_2_out), .in_0(rRAM_adr_Operand____accA), .in_1(1'b1), .out(multiplexer_12_out));
  Multiplexer #(.Bits(8)) multiplexer_13 (.sel(or_2_out), .in_0(newA), .in_1({8{1'b0}}), .out(multiplexer_13_out));
  D_FF d_ff_1 (.D(multiplexer_9_out), .C(clk), .Q(gf));  // open: nQ
  D_FF d_ff_2 (.D(multiplexer_8_out), .C(clk), .Q(lf));  // open: nQ
  xor xor_1 (xor_1_out, readyin, multiplexer_12_out);
  Multiplexer #(.Bits(8)) multiplexer_14 (
    .sel(FUTURE), .in_0(multiplexer_13_out), .in_1(Futureinput), .out(multiplexer_14_out));
  Multiplexer #(.Bits(8)) multiplexer_15 (
    .sel(switch_to_2), .in_0({4'b0000, Operand[3:0]}), .in_1({4'b0000, Operand[7:4]}),
    .out(multiplexer_15_out));
  D_FF d_ff_3 (.D(multiplexer_10_out), .C(clk), .Q(ef));  // open: nQ
  Multiplexer multiplexer_16 (.sel(result), .in_0(multiplexer_11_out), .in_1(result), .out(multiplexer_16_out));
  or or_4 (jump_if, Jump_to_address_Operand, and_1_out, and_2_out, and_3_out, and_4_out);
  D_FF d_ff_4 (.D(multiplexer_16_out), .C(clk), .Q(process_rRAM));  // open: nQ
  Multiplexer #(.Bits(8)) multiplexer_17 (
    .sel(FUTURE), .in_0(Operand), .in_1(multiplexer_15_out), .out(multiplexer_17_out));
  RAMDualAccess #(.AddrBits(8), .Bits(8)) rRAM (
    .str(xor_1_out), .C(clk), .ld(process_rRAM), .A1(multiplexer_3_out), .Din1(multiplexer_14_out),
    .A2(multiplexer_17_out), .D1(Output_t), .D2(rRAMout));
  or or_5 (or_5_out, reset, process_reset);
  xor xor_2 (xor_2_out, finishfuture, FUTURE);
  or or_6 (or_6_out, progLoad, process);
  xor xor_3 (xor_3_out, xor_2_out, or_6_out);
  or or_7 (or_7_out, reset, start);
  Delay delay_1 (.in(or_5_out), .out(delay_1_out));
  Multiplexer #(.Bits(8)) multiplexer_18 (.sel(process_rRAM), .in_0({8{1'b0}}), .in_1(Output_t), .out(\output ));
  Delay #(.Bits(13)) delay_2 (.in(progIN), .out(delay_2_out));
  or or_8 (or_8_out, done, end_reset);
  D_FF d_ff_5 (.D(multiplexer_21_out), .C(clk), .Q(valid));  // open: nQ
  Multiplexer #(.Bits(8)) multiplexer_19 (
    .sel(accA___pRAM_adr_Operand), .in_0({8{1'b0}}), .in_1(Operand), .out(multiplexer_19_out));
  CounterPreset #(.Bits(8)) counterpreset_2 (
    .en(xor_3_out), .C(clk), .dir(1'b0), .in(Operand), .ld(jump_if), .clr(or_7_out), .out(Adress),
    .ovf(out_15));
  CounterPreset #(.maxValue(15), .Bits(8)) counterpreset_3 (
    .en(delay_1_out), .C(clk), .dir(1'b0), .in(8'h1), .ld(1'b0), .clr(or_8_out), .out(Adress_3));  // open: ovf
  Multiplexer multiplexer_20 (.sel(stop), .in_0(valid), .in_1(stop), .out(multiplexer_20_out));
  Multiplexer multiplexer_21 (.sel(reset), .in_0(multiplexer_20_out), .in_1(1'b0), .out(multiplexer_21_out));
  and and_5 (and_5_out, \end , valid);
  RAMDualAccess #(.AddrBits(8), .Bits(13)) u_pRAM (
    .str(progLoad), .C(clk), .ld(process), .A1(Adress), .Din1(delay_2_out), .A2(multiplexer_19_out),
    .D1({Opcode, Operand}), .D2(pRAM));
  Comparator #(.Bits(8)) comparator_2 (.a(Adress_3), .b(8'hf), .eq(end_reset));  // open: gt, lt
  Multiplexer multiplexer_22 (.sel(\end ), .in_0(done), .in_1(and_5_out), .out(multiplexer_22_out));
  Seven_Seg_Hex seven_seg_hex_1 (.d(\output [7:4]), .dp(1'b0));
  Multiplexer multiplexer_23 (.sel(or_9_out), .in_0(multiplexer_22_out), .in_1(1'b0), .out(multiplexer_23_out));
  or or_9 (or_9_out, result, reset);
  Seven_Seg_Hex seven_seg_hex_2 (.d(\output [3:0]), .dp(1'b0));
  D_FF d_ff_6 (.D(multiplexer_23_out), .C(clk), .Q(done));  // open: nQ
  Multiplexer multiplexer_24 (.sel(stop), .in_0(process), .in_1(1'b0), .out(multiplexer_24_out));
  Multiplexer multiplexer_25 (.sel(start), .in_0(multiplexer_24_out), .in_1(start), .out(multiplexer_25_out));
  or or_10 (or_10_out, progLoad, end_reset);
  Multiplexer multiplexer_26 (.sel(or_10_out), .in_0(process_reset), .in_1(1'b0), .out(multiplexer_26_out));
  Multiplexer multiplexer_27 (.sel(reset), .in_0(multiplexer_26_out), .in_1(reset), .out(multiplexer_27_out));
  D_FF d_ff_7 (.D(multiplexer_25_out), .C(clk), .Q(process));  // open: nQ
  D_FF d_ff_8 (.D(multiplexer_27_out), .C(clk), .Q(process_reset));  // open: nQ
  Demultiplexer #(.Selector_Bits(5)) demultiplexer_1 (
    .sel(Opcode), .in(process), .out_1(accA___Operand), .out_2(accB___Operand), .out_3(accA___accB),
    .out_4(accB___accA), .out_5(regC___accA), .out_6(accA___regC), .out_7(regC___M), .out_8(regC___N),
    .out_9(accA___pRAM_adr_Operand), .out_10(accA___rRAM_adr_Operand), .out_11(rRAM_adr_Operand____accA),
    .out_12(Jump_to_address_Operand), .out_13(Jump_to_address_Operand_if_eq),
    .out_14(Jump_to_address_Operand_if_gr), .out_15(Jump_to_address_Operand_if_le),
    .out_16(Jump_to_address_Operand_if_eq_or_gr), .out_17(accA___accA__plus__accB),
    .out_18(accA___accA___accB_t_t), .out_19(accA___accA___accB_t), .out_20(accA___accA___accB_t_t_t),
    .out_21(accA___accA___accB), .out_22(accA___accA___accB_t_t_t_t), .out_23(accA_CMP_accB),
    .out_24(accA___NOT_accA), .out_25(accA____accA_AND_accB), .out_26(accA____accA_OR_accB),
    .out_27(accA____accA_XOR_accB), .out_28(accA____accA__lt__lt__accB), .out_29(isPrime_accA),
    .out_30(FUTURE), .out_31(stop));  // open: out_0
  Comparator #(.Signed("true"), .Bits(8)) comparator_3 (.a(out_16), .b(out_17), .gt(greather), .eq(equal), .lt(less));
  Add #(.Bits(8)) add_1 (.a(out_16), .b(out_17), .c_i(1'b0), .s(plus));  // open: c_o
  Sub #(.Bits(8)) sub_1 (.a(out_16), .b(out_17), .c_i(1'b0), .s(tunnel_t_t));  // open: c_o
  ROM #(.AddrBits(6), .Bits(8)) rom_1 (.A({out_16[2:0], out_17[2:0]}), .sel(1'b1), .D(tunnel_t_t_t_t));
  ROM #(.AddrBits(8)) isPrime (.A(out_16), .sel(1'b1), .D(prime));
  Multiplexer #(.Bits(8)) multiplexer_28 (.sel(reset), .in_0(newA), .in_1({8{1'b0}}), .out(multiplexer_28_out));
  Multiplexer multiplexer_29 (.sel(reset), .in_0(newA_if), .in_1(1'b1), .out(multiplexer_29_out));
  Multiplexer #(.Bits(8)) multiplexer_30 (.sel(reset), .in_0(newA), .in_1({8{1'b0}}), .out(multiplexer_30_out));
  Multiplexer multiplexer_31 (.sel(reset), .in_0(newB_if), .in_1(1'b1), .out(multiplexer_31_out));
  Multiplexer #(.Bits(8)) multiplexer_32 (.sel(reset), .in_0(newA), .in_1({8{1'b0}}), .out(multiplexer_32_out));
  Multiplexer multiplexer_33 (.sel(reset), .in_0(newC_if), .in_1(1'b1), .out(multiplexer_33_out));
  Mul #(.Bits(4)) mul_1 (.a(out_16[3:0]), .b(out_17[3:0]), .mul(tunnel_t));
  Div #(.Bits(8)) div_1 (.a(out_16), .b(out_17), .q(tunnel_t_t_t), .r(tunnel));
  Register #(.Bits(8)) accA (.D(multiplexer_28_out), .C(clk), .en(multiplexer_29_out), .Q(out_16));
  Register #(.Bits(8)) accB (.D(multiplexer_30_out), .C(clk), .en(multiplexer_31_out), .Q(out_17));
  Register #(.Bits(8)) RegC (.D(multiplexer_32_out), .C(clk), .en(multiplexer_33_out), .Q(out_18));
  assign \not  = out_16 ^ {8{1'b1}};  // XOr xor_4, 8 bits wide
  assign \and  = out_16 & out_17;  // And and_6, 8 bits wide
  assign \or  = out_16 | out_17;  // Or or_11, 8 bits wide
  assign \xor  = out_16 ^ out_17;  // XOr xor_5, 8 bits wide
  BarrelShifter #(.Bits(8)) barrelshifter_1 (.in(out_16), .shift({1'b0, out_17[2:0]}), .out(shift_left));
  Multiplexer #(.Selector_Bits(5), .Bits(8)) multiplexer_34 (
    .sel(Opcode), .in_0({8{1'b0}}), .in_1(Operand), .in_2(Operand), .in_3(out_17), .in_4(out_16),
    .in_5(out_16), .in_6(out_18), .in_7(M), .in_8(N), .in_9(pRAM[7:0]), .in_10(rRAMout), .in_11(out_16),
    .in_12({8{1'b0}}), .in_13({8{1'b0}}), .in_14({8{1'b0}}), .in_15({8{1'b0}}), .in_16({8{1'b0}}),
    .in_17(plus), .in_18(tunnel_t_t), .in_19(tunnel_t), .in_20(tunnel_t_t_t), .in_21(tunnel),
    .in_22(tunnel_t_t_t_t), .in_23({8{1'b0}}), .in_24(\not ), .in_25(\and ), .in_26(\or ), .in_27(\xor ),
    .in_28(shift_left), .in_29({8{1'b0}}), .in_30({8{1'b0}}), .in_31({8{1'b0}}), .out(newA));
  or or_12 (newB_if, accB___Operand, accB___accA);
  or or_13 (newC_if, regC___accA, regC___M, regC___N);
  or or_14 (newA_if, accA___Operand, accA___accB, accA___regC, accA___pRAM_adr_Operand, accA___rRAM_adr_Operand, accA___accA__plus__accB, accA___accA___accB_t_t, accA___accA___accB_t, accA___accA___accB_t_t_t, accA___accA___accB, accA___accA___accB_t_t_t_t, accA___NOT_accA, accA____accA_AND_accB, accA____accA_OR_accB, accA____accA_XOR_accB, accA____accA__lt__lt__accB);
  xor xor_6 (xor_6_out, FUTURE, switch_to_2);
  D_FF d_ff_9 (.D(multiplexer_35_out), .C(clk), .Q(switch_to_2));  // open: nQ
  Multiplexer multiplexer_35 (.sel(or_15_out), .in_0(xor_6_out), .in_1(1'b0), .out(multiplexer_35_out));
  Multiplexer multiplexer_36 (.sel(or_15_out), .in_0(switch_to_2), .in_1(1'b0), .out(multiplexer_36_out));
  Register #(.Bits(8)) u_m (.D(rRAMout), .C(clk), .en(multiplexer_35_out), .Q(m_2));
  Register #(.Bits(8)) u_n (.D(rRAMout), .C(clk), .en(multiplexer_36_out), .Q(n_2));
  Comparator #(.Bits(8)) comparator_4 (.a(n_2), .b({8{1'b0}}), .gt(comparator_4_gt), .lt(comparator_4_lt));  // open: eq
  or or_15 (or_15_out, comparator_4_gt, comparator_4_lt);
  ROM #(.AddrBits(16), .Bits(16)) rom_2 (.A({n_2, m_2}), .sel(1'b1), .D(rom_2_d));
  and and_7 (readyin, or_15_out, FUTURE);
  Multiplexer multiplexer_37 (.sel(or_15_out), .in_0(1'b0), .in_1(or_16_out), .out(multiplexer_37_out));
  D_FF d_ff_10 (.D(multiplexer_37_out), .C(clk), .Q(d_ff_10_q));  // open: nQ
  or or_16 (or_16_out, comparator_5_gt, comparator_5_lt);
  Add #(.Bits(8)) add_2 (.a(8'he), .b({8{1'b0}}), .c_i(d_ff_10_q), .s(Futureaddress));  // open: c_o
  Multiplexer #(.Bits(8)) multiplexer_38 (
    .sel(d_ff_10_q), .in_0(rom_2_d[15:8]), .in_1(rom_2_d[7:0]), .out(Futureinput));
  Comparator #(.Bits(8)) comparator_5 (
    .a(rom_2_d[7:0]), .b(rom_2_d[15:8]), .gt(comparator_5_gt), .lt(comparator_5_lt));  // open: eq
  D_FF d_ff_11 (.D(d_ff_10_q), .C(clk), .Q(finishfuture));  // open: nQ

  // Other names for the same wires on the sheet: accA_plus[7:0] = out_16; accB_plus[7:0] = out_17;
  //   counter[7:0] = Adress; counter_reset[7:0] = Adress_3; counter_rRAM[7:0] = Adress_2;
  //   RegC_plus__plus[7:0] = out_18; newB[7:0] = newA; newC[7:0] = newA; rRAMin[7:0] = newA

  // Notes on the sheet:
  //   counter_rRAM
  //   member
  //   rRam
  //   นาย อภิวิชญ์ แสงอังคนาวิน 6733289421
  //   นาย สุวิจักขณ์ ภู่ภักดีพันธ์ 6733280721
  //   นาย วิทูทรรศน์ ถิ่นพระบาท 6733243521
  //   นาย ภคพล ยอดชัยพฤกษ์ 6733187021
  //   jump_if
  //   flag
  //   process_rRAM
  //   counter_reset
  //   counter_pRAM
  //   PC
  //   process_pRAM
  //   process_reset
  //   Decoder
  //   ALU
  //   accA
  //   accB
  //   RegC
  //   contents of rom_1 (hex, n*v repeats v):
  //   1,7*0,9*1,2,4,8,10,20,40,80,1,3,9,1b,51,f3,2d9,88b,1,4,10,40,100
  //   ,400,0,0,1,5,19,7d,271,c35,3d09,1312d,1,6,24,d8,510,1e60,b640
  //   ,44580,1,7,31,157,961,41a7,1cb91,c90f7
  //   contents of isPrime (hex, n*v repeats v):
  //   0,0,1,1,0,1,0,1,0,0,0,1,0,1,0,0,0,1,0,1,0,0,0,1,5*0,1,0,1,5*0
  //   ,1,0,0,0,1,0,1,0,0,0,1,5*0,1,5*0,1,0,1,5*0,1,0,0,0,1,0,1,5*0,1
  //   ,0,0,0,1,5*0,1,7*0,1,0,0,0,1,0,1,0,0,0,1,0,1,0,0,0,1,13*0,1,0,0,0
  //   ,1,5*0,1,0,1,9*0,9,0,1,5*0,1,5*0,1,0,0,0,1,5*0,1,5*0,1,0,1,9*0
  //   ,1,0,1,0,0,0,1,0,1,11*0,1,11*0,1,0,0,0,1,0,1,0,0,0,1,5*0,1,0,1
  //   ,9*0,1
  //   selector
  //   newVariable_if
  //   Future
  //   contents of rom_2 (hex, n*v repeats v):
  //   5150*0,3c,43659*0,c9e
endmodule

/* Test case 01_P01T2:
M N progIN reset progLoad start result clk valid done output
0 0 0 0 0 0 0 0 0 0 0
0 0 0 0 0 0 0 1 0 0 0
0 0 0 1 0 0 0 0 0 0 0
0 0 0 1 0 0 0 1 0 0 0
0 0 0 0 0 0 0 0 0 0 0
0 0 0 0 0 0 0 1 0 0 0
0 0 0 0 0 0 0 0 0 0 0
0 0 0 0 0 0 0 1 0 0 0
0 0 0 0 0 0 0 0 0 0 0
0 0 0 0 0 0 0 1 0 0 0
0 0 0 0 0 0 0 0 0 0 0
0 0 0 0 0 0 0 1 0 0 0
0 0 0 0 0 0 0 0 0 0 0
0 0 0 0 0 0 0 1 0 0 0
0 0 0 0 0 0 0 0 0 0 0
0 0 0 0 0 0 0 1 0 0 0
0 0 0 0 0 0 0 0 0 0 0
0 0 0 0 0 0 0 1 0 0 0
0 0 0 0 0 0 0 0 0 0 0
0 0 0 0 0 0 0 1 0 0 0
0 0 0 0 0 0 0 0 0 0 0
0 0 0 0 0 0 0 1 0 0 0
0 0 0 0 0 0 0 0 0 0 0
0 0 0 0 0 0 0 1 0 0 0
0 0 0 0 0 0 0 0 0 0 0
0 0 0 0 0 0 0 1 0 0 0
0 0 0 0 0 0 0 0 0 0 0
0 0 0 0 0 0 0 1 0 0 0
0 0 0 0 0 0 0 0 0 0 0
0 0 0 0 0 0 0 1 0 0 0
0 0 0 0 0 0 0 0 0 0 0
0 0 0 0 0 0 0 1 0 0 0
0 0 0 0 0 0 0 0 0 0 0
0 0 0 0 0 0 0 1 0 0 0
0 0 0 0 0 0 0 0 0 0 0
0 0 0 0 0 0 0 1 0 0 0
0 0 0 0 0 0 0 0 0 0 0
0 0 0 0 0 0 0 1 0 0 0
0 0 0 0 0 0 0 0 0 0 0
0 0 0 0 0 0 0 1 0 0 0
0 0 0 0 0 0 0 0 0 0 0
0 0 0 0 0 0 0 1 0 0 0
0 0 271 0 1 0 0 0 0 0 0
0 0 0 0 1 0 0 1 0 0 0
0 0 565 0 1 0 0 0 0 0 0
0 0 0 0 1 0 0 1 0 0 0
0 0 4352 0 1 0 0 0 0 0 0
0 0 0 0 1 0 0 1 0 0 0
0 0 2819 0 1 0 0 0 0 0 0
0 0 0 0 1 0 0 1 0 0 0
0 0 7936 0 1 0 0 0 0 0 0
0 0 0 0 1 0 0 1 0 0 0
0 0 0 0 0 1 0 0 0 0 0
0 0 0 0 0 1 0 1 0 0 0
0 0 0 0 0 0 0 0 x 0 0
0 0 0 0 0 0 0 1 x 0 0
0 0 0 0 0 0 0 0 x 0 0
0 0 0 0 0 0 0 1 x 0 0
0 0 0 0 0 0 0 0 x 0 0
0 0 0 0 0 0 0 1 x 0 0
0 0 0 0 0 0 0 0 x 0 0
0 0 0 0 0 0 0 1 x 0 0
0 0 0 0 0 0 0 0 x 0 0
0 0 0 0 0 0 0 1 x 0 0
0 0 0 0 0 0 0 0 x 0 0
0 0 0 0 0 0 0 1 x 0 0
0 0 0 0 0 0 0 0 x 0 0
0 0 0 0 0 0 0 1 x 0 0
0 0 0 0 0 0 0 0 x 0 0
0 0 0 0 0 0 0 1 x 0 0
0 0 0 0 0 0 0 0 x 0 0
0 0 0 0 0 0 0 1 x 0 0
0 0 0 0 0 0 0 0 x 0 0
0 0 0 0 0 0 0 1 x 0 0
0 0 0 0 0 0 0 0 x 0 0
0 0 0 0 0 0 0 1 x 0 0
0 0 0 0 0 0 0 0 x 0 0
0 0 0 0 0 0 0 1 x 0 0
0 0 0 0 0 0 0 0 x 0 0
0 0 0 0 0 0 0 1 x 0 0
0 0 0 0 0 0 0 0 x 0 0
0 0 0 0 0 0 0 1 x 0 0
0 0 0 0 0 0 0 0 x 0 0
0 0 0 0 0 0 0 1 x 0 0
0 0 0 0 0 0 0 0 x 0 0
0 0 0 0 0 0 0 1 x 0 0
0 0 0 0 0 0 0 0 x 0 0
0 0 0 0 0 0 0 1 x 0 0
0 0 0 0 0 0 0 0 x 0 0
0 0 0 0 0 0 0 1 x 0 0
0 0 0 0 0 0 0 0 x 0 0
0 0 0 0 0 0 0 1 x 0 0
0 0 0 0 0 0 0 0 x 0 0
0 0 0 0 0 0 0 1 x 0 0
0 0 0 0 0 0 0 0 x 0 0
0 0 0 0 0 0 0 1 x 0 0
0 0 0 0 0 0 0 0 x 0 0
0 0 0 0 0 0 0 1 x 0 0
0 0 0 0 0 0 0 0 x 0 0
0 0 0 0 0 0 0 1 x 0 0
0 0 0 0 0 0 0 0 x 0 0
0 0 0 0 0 0 0 1 x 0 0
0 0 0 0 0 0 0 0 x 0 0
0 0 0 0 0 0 0 1 x 0 0
0 0 0 0 0 0 0 0 x 0 0
0 0 0 0 0 0 0 1 1 0 0
0 0 0 0 0 0 1 0 1 0 0
0 0 0 0 0 0 1 1 1 0 0
0 0 0 0 0 0 0 0 1 0 0
0 0 0 0 0 0 0 1 1 0 0
0 0 0 0 0 0 0 0 1 0 0
0 0 0 0 0 0 0 1 1 0 0
0 0 0 0 0 0 0 0 1 0 0
0 0 0 0 0 0 0 1 1 0 68
0 0 0 0 0 0 0 0 1 0 68
0 0 0 0 0 0 0 1 1 0 0
0 0 0 0 0 0 0 0 1 0 0
0 0 0 0 0 0 0 1 1 0 0
0 0 0 0 0 0 0 0 1 0 0
0 0 0 0 0 0 0 1 1 0 0
0 0 0 0 0 0 0 0 1 0 0
0 0 0 0 0 0 0 1 1 0 0
0 0 0 0 0 0 0 0 1 0 0
0 0 0 0 0 0 0 1 1 0 0
0 0 0 0 0 0 0 0 1 0 0
0 0 0 0 0 0 0 1 1 0 0
0 0 0 0 0 0 0 0 1 0 0
0 0 0 0 0 0 0 1 1 0 0
0 0 0 0 0 0 0 0 1 0 0
0 0 0 0 0 0 0 1 1 0 0
0 0 0 0 0 0 0 0 1 0 0
0 0 0 0 0 0 0 1 1 0 0
0 0 0 0 0 0 0 0 1 0 0
0 0 0 0 0 0 0 1 1 0 0
0 0 0 0 0 0 0 0 1 0 0
0 0 0 0 0 0 0 1 1 0 0
0 0 0 0 0 0 0 0 1 0 0
0 0 0 0 0 0 0 1 1 0 0
0 0 0 0 0 0 0 0 1 0 0
0 0 0 0 0 0 0 1 1 1 0
0 0 0 0 0 0 0 0 1 1 0
0 0 0 0 0 0 0 1 1 1 0
0 0 0 0 0 0 0 0 1 1 0
*/

/* Test case Jump:
M N progIN reset progLoad start result clk valid done output
0	0	0	0	0	0	0	0	x	x	x
0	0	0	0	0	0	0	1	x	x	x
0	0	0	1	0	0	0	0	x	x	x
0	0	0	1	0	0	0	1	0	0	0
0	0	0	0	0	0	0	0	0	0	0
0	0	0	0	0	0	0	1	0	0	0
0	0	0	0	0	0	0	0	0	0	0
0	0	0	0	0	0	0	1	0	0	0
0	0	0	0	0	0	0	0	0	0	0
0	0	0	0	0	0	0	1	0	0	0
0	0	0	0	0	0	0	0	0	0	0
0	0	0	0	0	0	0	1	0	0	0
0	0	0	0	0	0	0	0	0	0	0
0	0	0	0	0	0	0	1	0	0	0
0	0	0	0	0	0	0	0	0	0	0
0	0	0	0	0	0	0	1	0	0	0
0	0	0	0	0	0	0	0	0	0	0
0	0	0	0	0	0	0	1	0	0	0
0	0	0	0	0	0	0	0	0	0	0
0	0	0	0	0	0	0	1	0	0	0
0	0	0	0	0	0	0	0	0	0	0
0	0	0	0	0	0	0	1	0	0	0
0	0	0	0	0	0	0	0	0	0	0
0	0	0	0	0	0	0	1	0	0	0
0	0	0	0	0	0	0	0	0	0	0
0	0	0	0	0	0	0	1	0	0	0
0	0	0	0	0	0	0	0	0	0	0
0	0	0	0	0	0	0	1	0	0	0
0	0	0	0	0	0	0	0	0	0	0
0	0	0	0	0	0	0	1	0	0	0
0	0	0	0	0	0	0	0	0	0	0
0	0	0	0	0	0	0	1	0	0	0
0	0	0	0	0	0	0	0	0	0	0
0	0	0	0	0	0	0	1	0	0	0
0	0	0	0	0	0	0	0	0	0	0
0	0	0	0	0	0	0	1	0	0	0
0	0	0	0	0	0	0	0	0	0	0
0	0	0	0	0	0	0	1	0	0	0
0	0	0	0	0	0	0	0	0	0	0
0	0	0	0	0	0	0	1	0	0	0
0	0	0	0	0	0	0	0	0	0	0
0	0	0	0	0	0	0	1	0	0	0
0	0	271	0	1	0	0	0	0	0	0
0	0	271	0	1	0	0	1	0	0	0
0	0	566	0	1	0	0	0	0	0	0
0	0	566	0	1	0	0	1	0	0	0
0	0	5888	0	1	0	0	0	0	0	0
0	0	5888	0	1	0	0	1	0	0	0
0	0	3599	0	1	0	0	0	0	0	0
0	0	3599	0	1	0	0	1	0	0	0
0	0	4110	0	1	0	0	0	0	0	0
0	0	4110	0	1	0	0	1	0	0	0
0	0	3856	0	1	0	0	0	0	0	0
0	0	3856	0	1	0	0	1	0	0	0
0	0	0	0	1	0	0	0	0	0	0
0	0	0	0	1	0	0	1	0	0	0
0	0	0	0	1	0	0	0	0	0	0
0	0	0	0	1	0	0	1	0	0	0
0	0	0	0	1	0	0	0	0	0	0
0	0	0	0	1	0	0	1	0	0	0
0	0	0	0	1	0	0	0	0	0	0
0	0	0	0	1	0	0	1	0	0	0
0	0	0	0	1	0	0	0	0	0	0
0	0	0	0	1	0	0	1	0	0	0
0	0	0	0	1	0	0	0	0	0	0
0	0	0	0	1	0	0	1	0	0	0
0	0	0	0	1	0	0	0	0	0	0
0	0	0	0	1	0	0	1	0	0	0
0	0	0	0	1	0	0	0	0	0	0
0	0	0	0	1	0	0	1	0	0	0
0	0	0	0	1	0	0	0	0	0	0
0	0	0	0	1	0	0	1	0	0	0
0	0	0	0	1	0	0	0	0	0	0
0	0	0	0	1	0	0	1	0	0	0
0	0	4352	0	1	0	0	0	0	0	0
0	0	4352	0	1	0	0	1	0	0	0
0	0	2819	0	1	0	0	0	0	0	0
0	0	2819	0	1	0	0	1	0	0	0
0	0	7936	0	1	0	0	0	0	0	0
0	0	7936	0	1	0	0	1	0	0	0
0	0	0	0	1	0	0	0	0	0	0
0	0	0	0	1	0	0	1	0	0	0
0	0	0	0	0	0	0	0	0	0	0
0	0	0	0	0	0	0	1	0	0	0
0	0	0	0	0	0	0	0	0	0	0
0	0	0	0	0	0	0	1	0	0	0
0	0	0	0	0	0	0	0	0	0	0
0	0	0	0	0	0	0	1	0	0	0
0	0	0	0	0	1	0	0	0	0	0
0	0	0	0	0	1	0	1	0	0	0
0	0	0	0	0	0	0	0	x	0	0
0	0	0	0	0	0	0	1	x	0	0
0	0	0	0	0	0	0	0	x	0	0
0	0	0	0	0	0	0	1	x	0	0
0	0	0	0	0	0	0	0	x	0	0
0	0	0	0	0	0	0	1	x	0	0
0	0	0	0	0	0	0	0	x	0	0
0	0	0	0	0	0	0	1	x	0	0
0	0	0	0	0	0	0	0	x	0	0
0	0	0	0	0	0	0	1	x	0	0
0	0	0	0	0	0	0	0	x	0	0
0	0	0	0	0	0	0	1	x	0	0
0	0	0	0	0	0	0	0	x	0	0
0	0	0	0	0	0	0	1	x	0	0
0	0	0	0	0	0	0	0	x	0	0
0	0	0	0	0	0	0	1	x	0	0
0	0	0	0	0	0	0	0	x	0	0
0	0	0	0	0	0	0	1	x	0	0
0	0	0	0	0	0	0	0	x	0	0
0	0	0	0	0	0	0	1	x	0	0
0	0	0	0	0	0	0	0	x	0	0
0	0	0	0	0	0	0	1	x	0	0
0	0	0	0	0	0	0	0	x	0	0
0	0	0	0	0	0	0	1	x	0	0
0	0	0	0	0	0	0	0	x	0	0
0	0	0	0	0	0	0	1	x	0	0
0	0	0	0	0	0	0	0	x	0	0
0	0	0	0	0	0	0	1	x	0	0
0	0	0	0	0	0	0	0	x	0	0
0	0	0	0	0	0	0	1	x	0	0
0	0	0	0	0	0	0	0	x	0	0
0	0	0	0	0	0	0	1	x	0	0
0	0	0	0	0	0	0	0	x	0	0
0	0	0	0	0	0	0	1	x	0	0
0	0	0	0	0	0	0	0	x	0	0
0	0	0	0	0	0	0	1	x	0	0
0	0	0	0	0	0	0	0	x	0	0
0	0	0	0	0	0	0	1	x	0	0
0	0	0	0	0	0	0	0	x	0	0
0	0	0	0	0	0	0	1	x	0	0
0	0	0	0	0	0	0	0	x	0	0
0	0	0	0	0	0	0	1	x	0	0
0	0	0	0	0	0	0	0	x	0	0
0	0	0	0	0	0	0	1	x	0	0
0	0	0	0	0	0	0	0	x	0	0
0	0	0	0	0	0	0	1	x	0	0
0	0	0	0	0	0	0	0	x	0	0
0	0	0	0	0	0	0	1	x	0	0
0	0	0	0	0	0	0	0	x	0	0
0	0	0	0	0	0	0	1	x	0	0
0	0	0	0	0	0	0	0	x	0	0
0	0	0	0	0	0	0	1	1	0	0
0	0	0	0	0	0	1	0	1	0	0
0	0	0	0	0	0	1	1	1	0	0
0	0	0	0	0	0	0	0	1	0	0
0	0	0	0	0	0	0	1	1	0	0
0	0	0	0	0	0	0	0	1	0	0
0	0	0	0	0	0	0	1	1	0	0
0	0	0	0	0	0	0	0	1	0	0
0	0	0	0	0	0	0	1	1	0	69
0	0	0	0	0	0	0	0	1	0	69
0	0	0	0	0	0	0	1	1	0	0
0	0	0	0	0	0	0	0	1	0	0
0	0	0	0	0	0	0	1	1	0	0
0	0	0	0	0	0	0	0	1	0	0
0	0	0	0	0	0	0	1	1	0	0
0	0	0	0	0	0	0	0	1	0	0
0	0	0	0	0	0	0	1	1	0	0
0	0	0	0	0	0	0	0	1	0	0
0	0	0	0	0	0	0	1	1	0	0
0	0	0	0	0	0	0	0	1	0	0
0	0	0	0	0	0	0	1	1	0	0
0	0	0	0	0	0	0	0	1	0	0
0	0	0	0	0	0	0	1	1	0	0
0	0	0	0	0	0	0	0	1	0	0
0	0	0	0	0	0	0	1	1	0	0
0	0	0	0	0	0	0	0	1	0	0
0	0	0	0	0	0	0	1	1	0	0
0	0	0	0	0	0	0	0	1	0	0
0	0	0	0	0	0	0	1	1	0	0
0	0	0	0	0	0	0	0	1	0	0
0	0	0	0	0	0	0	1	1	0	0
0	0	0	0	0	0	0	0	1	0	0
0	0	0	0	0	0	0	1	1	0	0
0	0	0	0	0	0	0	0	1	0	0
0	0	0	0	0	0	0	1	1	1	0
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*/

/* Test case 09:
M	N	progIN	reset	progLoad	start	result	clk	valid	done	output
0	0	0	0	0	0	0	0	x	x	x
0	0	0	0	0	0	0	1	x	x	x
0	0	0	1	0	0	0	0	x	x	x
0	0	0	1	0	0	0	1	0	0	x
0	0	0	0	0	0	0	0	0	0	x
0	0	0	0	0	0	0	1	0	0	x
0	0	0	0	0	0	0	0	0	0	x
0	0	0	0	0	0	0	1	0	0	x
0	0	0	0	0	0	0	0	0	0	x
0	0	0	0	0	0	0	1	0	0	x
0	0	0	0	0	0	0	0	0	0	x
0	0	0	0	0	0	0	1	0	0	x
0	0	0	0	0	0	0	0	0	0	x
0	0	0	0	0	0	0	1	0	0	x
0	0	0	0	0	0	0	0	0	0	x
0	0	0	0	0	0	0	1	0	0	x
0	0	0	0	0	0	0	0	0	0	x
0	0	0	0	0	0	0	1	0	0	x
0	0	0	0	0	0	0	0	0	0	x
0	0	0	0	0	0	0	1	0	0	x
0	0	0	0	0	0	0	0	0	0	x
0	0	0	0	0	0	0	1	0	0	x
0	0	0	0	0	0	0	0	0	0	x
0	0	0	0	0	0	0	1	0	0	x
0	0	0	0	0	0	0	0	0	0	x
0	0	0	0	0	0	0	1	0	0	x
0	0	0	0	0	0	0	0	0	0	x
0	0	0	0	0	0	0	1	0	0	x
0	0	0	0	0	0	0	0	0	0	x
0	0	0	0	0	0	0	1	0	0	x
0	0	0	0	0	0	0	0	0	0	x
0	0	0	0	0	0	0	1	0	0	x
0	0	0	0	0	0	0	0	0	0	x
0	0	0	0	0	0	0	1	0	0	x
0	0	0	0	0	0	0	0	0	0	x
0	0	0	0	0	0	0	1	0	0	x
0	0	0	0	0	0	0	0	0	0	x
0	0	0	0	0	0	0	1	0	0	x
0	0	0	0	0	0	0	0	0	0	x
0	0	0	0	0	0	0	1	0	0	x
0	0	0	0	0	0	0	0	0	0	x
0	0	0	0	0	0	0	1	0	0	x
0	0	446	0	1	0	0	0	0	0	x
0	0	446	0	1	0	0	1	0	0	x
0	0	2817	0	1	0	0	0	0	0	x
0	0	2817	0	1	0	0	1	0	0	x
0	0	426	0	1	0	0	0	0	0	x
0	0	426	0	1	0	0	1	0	0	x
0	0	2831	0	1	0	0	0	0	0	x
0	0	2831	0	1	0	0	1	0	0	x
0	0	7711	0	1	0	0	0	0	0	x
0	0	7711	0	1	0	0	1	0	0	x
0	0	7936	0	1	0	0	0	0	0	x
0	0	7936	0	1	0	0	1	0	0	x
0	0	0	0	0	0	0	0	0	0	x
0	0	0	0	0	0	0	1	0	0	x
0	0	0	0	0	0	0	0	0	0	x
0	0	0	0	0	0	0	1	0	0	x
0	0	0	0	0	0	0	0	0	0	x
0	0	0	0	0	0	0	1	0	0	x
0	0	0	0	0	1	0	0	x	0	x
0	0	0	0	0	1	0	1	x	0	x
0	0	0	0	0	0	0	0	x	0	x
0	0	0	0	0	0	0	1	x	0	x
0	0	0	0	0	0	0	0	x	0	x
0	0	0	0	0	0	0	1	x	0	x
0	0	0	0	0	0	0	0	x	0	x
0	0	0	0	0	0	0	1	x	0	x
0	0	0	0	0	0	0	0	x	0	x
0	0	0	0	0	0	0	1	x	0	x
0	0	0	0	0	0	0	0	x	0	x
0	0	0	0	0	0	0	1	x	0	x
0	0	0	0	0	0	0	0	x	0	x
0	0	0	0	0	0	0	1	x	0	x
0	0	0	0	0	0	0	0	x	0	x
0	0	0	0	0	0	0	1	x	0	x
0	0	0	0	0	0	0	0	x	0	x
0	0	0	0	0	0	0	1	x	0	x
0	0	0	0	0	0	0	0	x	0	x
0	0	0	0	0	0	0	1	x	0	x
0	0	0	0	0	0	0	0	x	0	x
0	0	0	0	0	0	0	1	x	0	x
0	0	0	0	0	0	0	0	x	0	x
0	0	0	0	0	0	0	1	x	0	x
0	0	0	0	0	0	0	0	x	0	x
0	0	0	0	0	0	0	1	x	0	x
0	0	0	0	0	0	0	0	x	0	x
0	0	0	0	0	0	0	1	x	0	x
0	0	0	0	0	0	0	0	x	0	x
0	0	0	0	0	0	0	1	x	0	x
0	0	0	0	0	0	0	0	x	0	x
0	0	0	0	0	0	0	1	x	0	x
0	0	0	0	0	0	0	0	x	0	x
0	0	0	0	0	0	0	1	x	0	x
0	0	0	0	0	0	0	0	x	0	x
0	0	0	0	0	0	0	1	x	0	x
0	0	0	0	0	0	0	0	x	0	x
0	0	0	0	0	0	0	1	x	0	x
0	0	0	0	0	0	0	0	x	0	x
0	0	0	0	0	0	0	1	x	0	x
0	0	0	0	0	0	0	0	x	0	x
0	0	0	0	0	0	0	1	x	0	x
0	0	0	0	0	0	0	0	x	0	x
0	0	0	0	0	0	0	1	x	0	x
0	0	0	0	0	0	0	0	x	0	x
0	0	0	0	0	0	0	1	x	0	x
0	0	0	0	0	0	0	0	x	0	x
0	0	0	0	0	0	0	1	x	0	x
0	0	0	0	0	0	0	0	x	0	x
0	0	0	0	0	0	0	1	x	0	x
0	0	0	0	0	0	0	0	x	0	x
0	0	0	0	0	0	0	1	x	0	x
0	0	0	0	0	0	0	0	x	0	x
0	0	0	0	0	0	0	1	x	0	x
0	0	0	0	0	0	0	0	x	0	x
0	0	0	0	0	0	0	1	x	0	x
0	0	0	0	0	0	0	0	x	0	x
0	0	0	0	0	0	0	1	x	0	x
0	0	0	0	0	0	0	0	x	0	x
0	0	0	0	0	0	0	1	x	0	x
0	0	0	0	0	0	0	0	x	0	x
0	0	0	0	0	0	0	1	x	0	x
0	0	0	0	0	0	0	0	x	0	x
0	0	0	0	0	0	0	1	x	0	x
0	0	0	0	0	0	0	0	x	0	x
0	0	0	0	0	0	0	1	x	0	x
0	0	0	0	0	0	0	0	x	0	x
0	0	0	0	0	0	0	1	x	0	x
0	0	0	0	0	0	0	0	x	0	x
0	0	0	0	0	0	0	1	x	0	x
0	0	0	0	0	0	0	0	x	0	x
0	0	0	0	0	0	0	1	x	0	x
0	0	0	0	0	0	0	0	x	0	x
0	0	0	0	0	0	0	1	x	0	x
0	0	0	0	0	0	0	0	x	0	x
0	0	0	0	0	0	0	1	x	0	x
0	0	0	0	0	0	0	0	x	0	x
0	0	0	0	0	0	0	1	x	0	x
0	0	0	0	0	0	0	0	x	0	x
0	0	0	0	0	0	0	1	x	0	x
0	0	0	0	0	0	0	0	x	0	x
0	0	0	0	0	0	0	1	x	0	x
0	0	0	0	0	0	0	0	x	0	x
0	0	0	0	0	0	0	1	x	0	x
0	0	0	0	0	0	0	0	x	0	x
0	0	0	0	0	0	0	1	x	0	x
0	0	0	0	0	0	0	0	x	0	x
0	0	0	0	0	0	0	1	x	0	x
0	0	0	0	0	0	0	0	x	0	x
0	0	0	0	0	0	0	1	x	0	x
0	0	0	0	0	0	0	0	x	0	x
0	0	0	0	0	0	0	1	x	0	x
0	0	0	0	0	0	0	0	x	0	x
0	0	0	0	0	0	0	1	x	0	x
0	0	0	0	0	0	0	0	x	0	x
0	0	0	0	0	0	0	1	x	0	x
0	0	0	0	0	0	0	0	x	0	x
0	0	0	0	0	0	0	1	x	0	x
0	0	0	0	0	0	0	0	x	0	x
0	0	0	0	0	0	0	1	x	0	x
0	0	0	0	0	0	0	0	x	0	x
0	0	0	0	0	0	0	1	x	0	x
0	0	0	0	0	0	0	0	x	0	x
0	0	0	0	0	0	0	1	x	0	x
0	0	0	0	0	0	0	0	x	0	x
0	0	0	0	0	0	0	1	x	0	x
0	0	0	0	0	0	0	0	x	0	x
0	0	0	0	0	0	0	1	x	0	x
0	0	0	0	0	0	0	0	x	0	x
0	0	0	0	0	0	0	1	x	0	x
0	0	0	0	0	0	0	0	x	0	x
0	0	0	0	0	0	0	1	x	0	x
0	0	0	0	0	0	0	0	x	0	x
0	0	0	0	0	0	0	1	x	0	x
0	0	0	0	0	0	0	0	x	0	x
0	0	0	0	0	0	0	1	x	0	x
0	0	0	0	0	0	0	0	x	0	x
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*/

/* Test case:
M	N	progIN	reset	progLoad	start	result	clk	valid	done	output
0	0	0	0	0	0	0	0	x	x	x
0	0	0	0	0	0	0	1	x	x	x
0	0	0	1	0	0	0	0	x	x	x
0	0	0	1	0	0	0	1	0	0	x
0	0	0	0	0	0	0	0	0	0	x
0	0	0	0	0	0	0	1	0	0	x
0	0	0	0	0	0	0	0	0	0	x
0	0	0	0	0	0	0	1	0	0	x
0	0	0	0	0	0	0	0	0	0	x
0	0	0	0	0	0	0	1	0	0	x
0	0	0	0	0	0	0	0	0	0	x
0	0	0	0	0	0	0	1	0	0	x
0	0	0	0	0	0	0	0	0	0	x
0	0	0	0	0	0	0	1	0	0	x
0	0	0	0	0	0	0	0	0	0	x
0	0	0	0	0	0	0	1	0	0	x
0	0	0	0	0	0	0	0	0	0	x
0	0	0	0	0	0	0	1	0	0	x
0	0	0	0	0	0	0	0	0	0	x
0	0	0	0	0	0	0	1	0	0	x
0	0	0	0	0	0	0	0	0	0	x
0	0	0	0	0	0	0	1	0	0	x
0	0	0	0	0	0	0	0	0	0	x
0	0	0	0	0	0	0	1	0	0	x
0	0	0	0	0	0	0	0	0	0	x
0	0	0	0	0	0	0	1	0	0	x
0	0	0	0	0	0	0	0	0	0	x
0	0	0	0	0	0	0	1	0	0	x
0	0	0	0	0	0	0	0	0	0	x
0	0	0	0	0	0	0	1	0	0	x
0	0	0	0	0	0	0	0	0	0	x
0	0	0	0	0	0	0	1	0	0	x
0	0	0	0	0	0	0	0	0	0	x
0	0	0	0	0	0	0	1	0	0	x
0	0	0	0	0	0	0	0	0	0	x
0	0	0	0	0	0	0	1	0	0	x
0	0	0	0	0	0	0	0	0	0	x
0	0	0	0	0	0	0	1	0	0	x
0	0	0	0	0	0	0	0	0	0	x
0	0	0	0	0	0	0	1	0	0	x
0	0	0	0	0	0	0	0	0	0	x
0	0	0	0	0	0	0	1	0	0	x
0	0	276	0	1	0	0	0	0	0	x
0	0	276	0	1	0	0	1	0	0	x
0	0	2816	0	1	0	0	0	0	0	x
0	0	2816	0	1	0	0	1	0	0	x
0	0	286	0	1	0	0	0	0	0	x
0	0	286	0	1	0	0	1	0	0	x
0	0	2821	0	1	0	0	0	0	0	x
0	0	2821	0	1	0	0	1	0	0	x
0	0	7685	0	1	0	0	0	0	0	x
0	0	7685	0	1	0	0	1	0	0	x
0	0	7936	0	1	0	0	0	0	0	x
0	0	7936	0	1	0	0	1	0	0	x
0	0	0	0	0	0	0	0	0	0	x
0	0	0	0	0	0	0	1	0	0	x
0	0	0	0	0	0	0	0	0	0	x
0	0	0	0	0	0	0	1	0	0	x
0	0	0	0	0	0	0	0	0	0	x
0	0	0	0	0	0	0	1	0	0	x
0	0	0	0	0	1	0	0	x	0	x
0	0	0	0	0	1	0	1	x	0	x
0	0	0	0	0	0	0	0	x	0	x
0	0	0	0	0	0	0	1	x	0	x
0	0	0	0	0	0	0	0	x	0	x
0	0	0	0	0	0	0	1	x	0	x
0	0	0	0	0	0	0	0	x	0	x
0	0	0	0	0	0	0	1	x	0	x
0	0	0	0	0	0	0	0	x	0	x
0	0	0	0	0	0	0	1	x	0	x
0	0	0	0	0	0	0	0	x	0	x
0	0	0	0	0	0	0	1	x	0	x
0	0	0	0	0	0	0	0	x	0	x
0	0	0	0	0	0	0	1	x	0	x
0	0	0	0	0	0	0	0	x	0	x
0	0	0	0	0	0	0	1	x	0	x
0	0	0	0	0	0	0	0	x	0	x
0	0	0	0	0	0	0	1	x	0	x
0	0	0	0	0	0	0	0	x	0	x
0	0	0	0	0	0	0	1	x	0	x
0	0	0	0	0	0	0	0	x	0	x
0	0	0	0	0	0	0	1	x	0	x
0	0	0	0	0	0	0	0	x	0	x
0	0	0	0	0	0	0	1	x	0	x
0	0	0	0	0	0	0	0	x	0	x
0	0	0	0	0	0	0	1	x	0	x
0	0	0	0	0	0	0	0	x	0	x
0	0	0	0	0	0	0	1	x	0	x
0	0	0	0	0	0	0	0	x	0	x
0	0	0	0	0	0	0	1	x	0	x
0	0	0	0	0	0	0	0	x	0	x
0	0	0	0	0	0	0	1	x	0	x
0	0	0	0	0	0	0	0	x	0	x
0	0	0	0	0	0	0	1	x	0	x
0	0	0	0	0	0	0	0	x	0	x
0	0	0	0	0	0	0	1	x	0	x
0	0	0	0	0	0	0	0	x	0	x
0	0	0	0	0	0	0	1	x	0	x
0	0	0	0	0	0	0	0	x	0	x
0	0	0	0	0	0	0	1	x	0	x
0	0	0	0	0	0	0	0	x	0	x
0	0	0	0	0	0	0	1	x	0	x
0	0	0	0	0	0	0	0	x	0	x
0	0	0	0	0	0	0	1	x	0	x
0	0	0	0	0	0	0	0	x	0	x
0	0	0	0	0	0	0	1	x	0	x
0	0	0	0	0	0	0	0	x	0	x
0	0	0	0	0	0	0	1	x	0	x
0	0	0	0	0	0	0	0	x	0	x
0	0	0	0	0	0	0	1	x	0	x
0	0	0	0	0	0	0	0	x	0	x
0	0	0	0	0	0	0	1	x	0	x
0	0	0	0	0	0	0	0	x	0	x
0	0	0	0	0	0	0	1	x	0	x
0	0	0	0	0	0	0	0	x	0	x
0	0	0	0	0	0	0	1	x	0	x
0	0	0	0	0	0	0	0	x	0	x
0	0	0	0	0	0	0	1	x	0	x
0	0	0	0	0	0	0	0	x	0	x
0	0	0	0	0	0	0	1	x	0	x
0	0	0	0	0	0	0	0	x	0	x
0	0	0	0	0	0	0	1	x	0	x
0	0	0	0	0	0	0	0	x	0	x
0	0	0	0	0	0	0	1	x	0	x
0	0	0	0	0	0	0	0	x	0	x
0	0	0	0	0	0	0	1	x	0	x
0	0	0	0	0	0	0	0	x	0	x
0	0	0	0	0	0	0	1	x	0	x
0	0	0	0	0	0	0	0	x	0	x
0	0	0	0	0	0	0	1	x	0	x
0	0	0	0	0	0	0	0	x	0	x
0	0	0	0	0	0	0	1	x	0	x
0	0	0	0	0	0	0	0	x	0	x
0	0	0	0	0	0	0	1	x	0	x
0	0	0	0	0	0	0	0	x	0	x
0	0	0	0	0	0	0	1	x	0	x
0	0	0	0	0	0	0	0	x	0	x
0	0	0	0	0	0	0	1	x	0	x
0	0	0	0	0	0	0	0	x	0	x
0	0	0	0	0	0	0	1	x	0	x
0	0	0	0	0	0	0	0	x	0	x
0	0	0	0	0	0	0	1	x	0	x
0	0	0	0	0	0	0	0	x	0	x
0	0	0	0	0	0	0	1	x	0	x
0	0	0	0	0	0	0	0	x	0	x
0	0	0	0	0	0	0	1	x	0	x
0	0	0	0	0	0	0	0	x	0	x
0	0	0	0	0	0	0	1	x	0	x
0	0	0	0	0	0	0	0	x	0	x
0	0	0	0	0	0	0	1	x	0	x
0	0	0	0	0	0	0	0	x	0	x
0	0	0	0	0	0	0	1	x	0	x
0	0	0	0	0	0	0	0	x	0	x
0	0	0	0	0	0	0	1	x	0	x
0	0	0	0	0	0	0	0	x	0	x
0	0	0	0	0	0	0	1	x	0	x
0	0	0	0	0	0	0	0	x	0	x
0	0	0	0	0	0	0	1	x	0	x
0	0	0	0	0	0	0	0	x	0	x
0	0	0	0	0	0	0	1	x	0	x
0	0	0	0	0	0	0	0	x	0	x
0	0	0	0	0	0	0	1	x	0	x
0	0	0	0	0	0	0	0	x	0	x
0	0	0	0	0	0	0	1	x	0	x
0	0	0	0	0	0	0	0	x	0	x
0	0	0	0	0	0	0	1	x	0	x
0	0	0	0	0	0	0	0	x	0	x
0	0	0	0	0	0	0	1	x	0	x
0	0	0	0	0	0	0	0	x	0	x
0	0	0	0	0	0	0	1	x	0	x
0	0	0	0	0	0	0	0	x	0	x
0	0	0	0	0	0	0	1	x	0	x
0	0	0	0	0	0	0	0	x	0	x
0	0	0	0	0	0	0	1	x	0	x
0	0	0	0	0	0	0	0	x	0	x
0	0	0	0	0	0	0	1	x	0	x
0	0	0	0	0	0	0	0	x	0	x
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*/
